# Fritzing sketch TheKnob (saved by Fritzing 0.9.3b)
breadboards: 2

parts:
  D2 = Diode [package=diode-1n4148]
  D3 = Diode [package=diode-1n4148]
  D4 = Diode [package=diode-1n4148]
  D5 = Diode [package=diode-1n4148]
  D6 = Diode [package=diode-1n4148]
  D7 = Diode [package=diode-1n4148]
  D8 = Diode [package=diode-1n4148]
  D9 = Diode [package=diode-1n4148]
  D10 = Diode [package=diode-1n4148]
  U1 = SN74LS14N [package="DIP14 [THT]"]
  U5 = SN74LS32N [package="DIP14 [THT]"]
  U6 = SN74LS32N [package="DIP14 [THT]"]
  U7 = SN74LS32N [package="DIP14 [THT]"]
  U8 = SN74LS32N [package="DIP14 [THT]"]
  U3 = SN74LS14N [package="DIP14 [THT]"]
  U9 = SN74LS32N [package="DIP14 [THT]"]
  U10 = SN74LS32N [package="DIP14 [THT]"]
  U4 = SN74LS14N [package="DIP14 [THT]"]
  U11 = RF-LINK_TX [package=rf-link_tx]
  C4 = Electrolytic Capacitor [capacitance=100µF package="200 mil [THT, electrolytic]"]
  C3 = Electrolytic Capacitor [capacitance=100µF package="200 mil [THT, electrolytic]"]
  C2 = Electrolytic Capacitor [capacitance=47µF package="0807 [SMD, electrolytic]"]
  LED2 = smd LED [color="Red (633nm)" package="1206 [SMD]"]
  R1 = Resistor [tolerance=±5% resistance=330 package="0805 [SMD]"]
  R2 = Resistor [tolerance=±5% resistance=330 package="0805 [SMD]"]
  C1 = Electrolytic Capacitor [capacitance=47µF package="0807 [SMD, electrolytic]"]
  LED1 = smd LED [color="Red (633nm)" package="1206 [SMD]"]
  MOTOR1 = Adafruit Gear-Reduced Stepper Motor (small)
  U2 = SN74LS14N [package="DIP14 [THT]"]

nets:
  GND: D2.A, D3.A, D5.A, D7.A, D8.A, U1.GND, U5.GND, U6.GND, U7.GND, U8.GND, U8.3A, U3.GND, U9.GND, U10.GND, U4.GND, U11.GND, C4.-, C3.-, C2.-, LED2.cathode, C1.-, LED1.cathode, U2.GND, U2.4A
  N1: D2.C, D3.C, D4.A, U1.1A, MOTOR1.PINK
  VCC: D4.C, D6.C, D9.C, D10.C, U1.VCC, U5.Vcc, U6.Vcc, U7.Vcc, U8.Vcc, U3.VCC, U9.Vcc, U10.Vcc, U4.VCC, U11.+5V, C4.+, C3.+, U2.VCC
  N2: D5.C, D6.A, U1.6A, U5.3B, MOTOR1.YELLOW
  N3: D7.C, D9.A, U1.2A, MOTOR1.BLUE
  N4: D8.C, D10.A, U1.5A, U5.1A, MOTOR1.ORANGE
  N5: U1.1Y, U5.2A
  N6: U1.2Y, U5.2B
  N7: U1.3A, U5.1Y
  N8: U1.3Y, U6.1A
  N9: U1.4Y, U6.4B, U9.2B
  N10: U1.4A, U5.3Y
  N11: U1.5Y, U5.3A, U5.4A
  N12: U1.6Y, U5.1B, U5.4B
  N13: U5.2Y, U2.3A
  N14: U5.4Y, U7.1B, U7.4B, U2.5A
  N15: U6.1B, U6.4A, U2.1Y
  N16: U6.1Y, U6.2A
  N17: U6.2B, U7.1Y, U7.2B
  N18: U6.2Y, U7.1A, U3.2A, U2.2A
  N19: U6.3Y, U7.4A, U9.2A, U2.6A
  N20: U6.3A, U7.2A, U7.4Y
  N21: U6.3B, U6.4Y
  N22: U7.2Y, U2.1A
  N23: U7.3Y, U10.1A, U10.2B
  N24: U7.3A, U2.3Y
  N25: U7.3B, U2.5Y
  N26: U8.1A, U10.1B, U2.2Y
  N27: U8.1B, U8.2Y
  N28: U8.1Y, U8.2A, R1.Pin_0
  N29: U8.2B, U4.2Y
  N30: U8.3Y, U8.4A
  N31: U8.3B, U8.4Y, R2.Pin_0
  N32: U8.4B, U2.6Y
  N33: U3.2Y, U9.1B
  N34: U9.1A, U9.2Y
  N35: U9.1Y, U11.DATA
  N36: U10.1Y, U4.3A
  N37: U10.2Y, U4.2A
  N38: C2.+, LED2.anode, R1.Pin_1
  N39: R2.Pin_1, C1.+, LED1.anode

notes:
  The Knob with LED & RF:
  U1-4 = SN74HC04N
  U5-10 = SN74HC00N
  D1-9 = 1N4148
  C1-2 = 47µF
  C3-4 = 470µF
  R1-2 = 330Ω
  LED1-2 = L-934LSRD
  Motor = 28BYJ-48
  RF TWS-BS-3_433.92MHz
  The Knob
  Wireless battery-free knob with direction detection logic

custom parts:
  Diode: Diode These are standard reverse protection diodes and small signal diodes. SMA package can handle up to about 1A. SOD-323 can handle about 200mA. What the SOD-323 package when ordering, there are some mfgs out there that are 5-pin packages.
  Adafruit Gear-Reduced Stepper Motor (small): Adafruit gear-reduction stepper motor (small)
