# Fritzing sketch TheKnobReceiver (saved by Fritzing 0.9.3b)
breadboards: 1

parts:
  Part1 = Adafruit T-Cobbler Plus [part_number="Adafruit #1989 and #2028"]
  U1 = RF-LINK_RX [package=rf-link_rx]
  C1 = Electrolytic Capacitor [capacitance=47µF package="0807 [SMD, electrolytic]"]
  R1 = Resistor [tolerance=±5% resistance=510k package="0805 [SMD]"]
  R3 = Resistor [tolerance=±5% resistance=1.0M package="0805 [SMD]"]
  R4 = Resistor [tolerance=±5% resistance=4.3M package="0805 [SMD]"]
  U1_2 = SN74LS14N [package="DIP14 [THT]"]
  SPI_SSD1 = OLED 0.95" 96x64 SPI SSD1331
  R2 = Resistor [tolerance=±5% resistance=1.0M package="0805 [SMD]"]

nets:
  VCC: Part1.+3.3V, U1_2.VCC, SPI_SSD1.VCC
  GND: Part1.GND, U1.GND, C1.-, R3.Pin_0, R4.Pin_0, U1_2.1A, U1_2.GND, U1_2.4A, U1_2.5A, U1_2.6A, SPI_SSD1.GND
  N1: Part1.MOSI, SPI_SSD1.DIN
  N2: Part1.SCLK, SPI_SSD1.CLK
  N3: Part1.GPIO13, U1_2.2Y
  N4: Part1.GPIO26, U1_2.3Y
  +5V: Part1.+5V, U1.+5V, C1.+
  N5: Part1.GPIO23, SPI_SSD1.CS
  N6: Part1.GPIO24, SPI_SSD1.D/C
  N7: Part1.GPIO25, SPI_SSD1.RES
  N8: R1.Pin_1, U1_2.2A, R2.Pin_0
  N9: R3.Pin_1, R4.Pin_1, U1_2.3A, R2.Pin_1

notes:
  The Knob Receiver
  Wireless battery-free knob with direction detection logic
  The Knob RF Receiver with OLED display:
  U1 = SN74HC04N
  C1 = 47µF
  R1 = 510kΩ
  R2-3 = 1.0MΩ
  R4 = 4.3MΩ
  OLED = 0.95" SSD1331
  RF RWS-371-6_433.92MHz
  (Adafruit T-Cobbler Plus)

custom parts:
  Adafruit T-Cobbler Plus: The Raspberry Pi has landed on the Maker World like a 40-GPIO pinned, quad-USB ported, credit card sized bomb of DIY joy. And while you can use most of our great Model B accessories by hooking up our downgrade cable, its probably a good time to upgrade your set up and accessorize using all of the 40 pins. That's why we now carry the Assembled Adafruit Pi T-Cobbler Plus - Breakout + Cable for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
